# Fritzing sketch DisplayServer-print (saved by Fritzing 0.9.2b)
stripboards: 1

parts:
  ESP-1 = ESP-201
  RST = Pushbutton [package="[SMD]"]
  Prog = male pin header, 2 pins [form="♂ (male)"]
  SCL/SDA/VCC/GND = male pin header, 4 pins [form="♂ (male)"]
  C2 = Tantalum Capacitor [capacitance=10µF package="A 3216 [SMD, tantalum]"]
  3v3 = male pin header, 2 pins [form="♂ (male)"]
  S1 = Round Pushbutton
  S2 = Round Pushbutton
  IC1 = V_REG_LD1117VXX [package=78xxl]
  J1 = Power Jack [package=power_jack_combo]
  SG1 = Buzzer 12mm [package=buzzer-ccv]
  C3 = Tantalum Capacitor [capacitance=10µF package="A 3216 [SMD, tantalum]"]

nets:
  N1: ESP-1.IO0, Prog.pin1
  N2: ESP-1.IO2, SCL/SDA/VCC/GND.pin1
  N3: ESP-1.IO4, SCL/SDA/VCC/GND.pin2
  N4: ESP-1.3.3V, ESP-1.CHIP_EN, 3v3.pin1
  GND: ESP-1.GND, ESP-1.IO15, RST.Pin_1, RST.Pin_2, Prog.pin2, SCL/SDA/VCC/GND.pin4, C2.-, S1.leg1, S2.leg1, IC1.GND, J1.GND, C3.-
  N5: ESP-1.RST, RST.Pin_3, RST.Pin_4
  N6: ESP-1.IO14, SG1.2
  N7: ESP-1.IO12, S2.leg0
  N8: ESP-1.IO13, S1.leg0
  N9: SCL/SDA/VCC/GND.pin3, IC1.IN, J1.PWR, SG1.1, C3.+
  N10: C2.+, 3v3.pin2, IC1.OUT

custom parts:
  ESP-201: ESP-201 board with ESP8266 SoC with onboard wifi and antenna. This variant has the 4-pin serial connector moved to the top of the board, to make it breadboard-friendly.
