# Fritzing sketch DisplayServerIotsa (saved by Fritzing 0.9.3b)

parts:
  Part1 = iotsa esp-12 experiment board
  S1 = Square Pushbutton
  S2 = Square Pushbutton
  J1 = female pin header, 4 pins [form="♀ (female)"]  # not connected
  J2 = Piezo Speaker  # not connected

nets:
  N1: Part1.pin_10, Part1.pin_47, Part1.pin_48
  N2: Part1.pin_11, Part1.pin_51, Part1.pin_52
  N3: Part1.pin_13, Part1.pin_95, Part1.pin_97
  N4: Part1.pin_15, S2.leg0
  N5: Part1.pin_16, S1.leg0
  N6: Part1.pin_29, Part1.pin_53, Part1.pin_54
  N7: Part1.pin_37, Part1.pin_38, Part1.pin_39, Part1.pin_44, Part1.pin_57, Part1.pin_58, Part1.pin_104, Part1.pin_106, S1.leg1, S2.leg1

custom parts:
  iotsa esp-12 experiment board: Board with an ESP-12, a power supply, reset button, FTDI plug and experiment area.
